// Logisim project trab SD.circ as structural Verilog: 4 circuits, main circuit main
module main (
  input  [7:0] in_1,
  input  [7:0] in_2,
  output [9:0] out_3,
  output [11:0] out_4
);

  wire \multiplicador_mínimo_1_out_7 , \multiplicador_mínimo_2_out_7 , \multiplicador_mínimo_3_out_7 ,
       \multiplicador_mínimo_4_out_7 , \multiplicador_mínimo_5_out_7 , \multiplicador_mínimo_6_out_7 ,
       \multiplicador_mínimo_7_out_7 , \multiplicador_mínimo_9_out_7 , \multiplicador_mínimo_10_out_7 ,
       \multiplicador_mínimo_11_out_7 , \multiplicador_mínimo_12_out_7 , \multiplicador_mínimo_13_out_7 ,
       \multiplicador_mínimo_14_out_7 , \multiplicador_mínimo_15_out_7 ;

  and and_1 (out_3[0], in_1[0], in_2[0]);
  \multiplicador_mínimo  \multiplicador_mínimo_1  (
    .in_3(in_1[1]), .in_4(in_1[0]), .in_5(in_2[1]), .out_6(out_3[1]), .in_1(1'b0),
    .out_7(\multiplicador_mínimo_1_out_7 ), .in_2(in_2[0]));
  \multiplicador_mínimo  \multiplicador_mínimo_2  (
    .in_3(in_1[2]), .in_4(in_1[1]), .in_5(in_2[1]), .out_6(out_3[2]), .in_1(\multiplicador_mínimo_1_out_7 ),
    .out_7(\multiplicador_mínimo_2_out_7 ), .in_2(in_2[0]));
  \multiplicador_mínimo  \multiplicador_mínimo_3  (
    .in_3(in_1[3]), .in_4(in_1[2]), .in_5(in_2[1]), .out_6(out_3[3]), .in_1(\multiplicador_mínimo_2_out_7 ),
    .out_7(\multiplicador_mínimo_3_out_7 ), .in_2(in_2[0]));
  \multiplicador_mínimo  \multiplicador_mínimo_4  (
    .in_3(in_1[4]), .in_4(in_1[3]), .in_5(in_2[1]), .out_6(out_3[4]), .in_1(\multiplicador_mínimo_3_out_7 ),
    .out_7(\multiplicador_mínimo_4_out_7 ), .in_2(in_2[0]));
  \multiplicador_mínimo  \multiplicador_mínimo_5  (
    .in_3(in_1[5]), .in_4(in_1[4]), .in_5(in_2[1]), .out_6(out_3[5]), .in_1(\multiplicador_mínimo_4_out_7 ),
    .out_7(\multiplicador_mínimo_5_out_7 ), .in_2(in_2[0]));
  \multiplicador_mínimo  \multiplicador_mínimo_6  (
    .in_3(in_1[6]), .in_4(in_1[5]), .in_5(in_2[1]), .out_6(out_3[6]), .in_1(\multiplicador_mínimo_5_out_7 ),
    .out_7(\multiplicador_mínimo_6_out_7 ), .in_2(in_2[0]));
  \multiplicador_mínimo  \multiplicador_mínimo_7  (
    .in_3(in_1[7]), .in_4(in_1[6]), .in_5(in_2[1]), .out_6(out_3[7]), .in_1(\multiplicador_mínimo_6_out_7 ),
    .out_7(\multiplicador_mínimo_7_out_7 ), .in_2(in_2[0]));
  \multiplicador_mínimo  \multiplicador_mínimo_8  (
    .in_3(in_1[6]), .in_4(1'b0), .in_5(1'b0), .out_6(out_3[8]), .in_1(\multiplicador_mínimo_7_out_7 ),
    .out_7(out_3[9]), .in_2(in_2[0]));
  and and_2 (out_4[2], in_1[0], in_2[0]);
  \multiplicador_mínimo  \multiplicador_mínimo_9  (
    .in_3(in_1[1]), .in_4(in_1[0]), .in_5(in_2[1]), .out_6(out_4[3]), .in_1(1'b0),
    .out_7(\multiplicador_mínimo_9_out_7 ), .in_2(in_2[0]));
  \multiplicador_mínimo  \multiplicador_mínimo_10  (
    .in_3(in_1[2]), .in_4(in_1[1]), .in_5(in_2[1]), .out_6(out_4[4]), .in_1(\multiplicador_mínimo_9_out_7 ),
    .out_7(\multiplicador_mínimo_10_out_7 ), .in_2(in_2[0]));
  \multiplicador_mínimo  \multiplicador_mínimo_11  (
    .in_3(in_1[3]), .in_4(in_1[2]), .in_5(in_2[1]), .out_6(out_4[5]), .in_1(\multiplicador_mínimo_10_out_7 ),
    .out_7(\multiplicador_mínimo_11_out_7 ), .in_2(in_2[0]));
  \multiplicador_mínimo  \multiplicador_mínimo_12  (
    .in_3(in_1[4]), .in_4(in_1[3]), .in_5(in_2[1]), .out_6(out_4[6]), .in_1(\multiplicador_mínimo_11_out_7 ),
    .out_7(\multiplicador_mínimo_12_out_7 ), .in_2(in_2[0]));
  \multiplicador_mínimo  \multiplicador_mínimo_13  (
    .in_3(in_1[5]), .in_4(in_1[4]), .in_5(in_2[1]), .out_6(out_4[7]), .in_1(\multiplicador_mínimo_12_out_7 ),
    .out_7(\multiplicador_mínimo_13_out_7 ), .in_2(in_2[0]));
  \multiplicador_mínimo  \multiplicador_mínimo_14  (
    .in_3(in_1[6]), .in_4(in_1[5]), .in_5(in_2[1]), .out_6(out_4[8]), .in_1(\multiplicador_mínimo_13_out_7 ),
    .out_7(\multiplicador_mínimo_14_out_7 ), .in_2(in_2[0]));
  \multiplicador_mínimo  \multiplicador_mínimo_15  (
    .in_3(in_1[7]), .in_4(in_1[6]), .in_5(in_2[1]), .out_6(out_4[9]), .in_1(\multiplicador_mínimo_14_out_7 ),
    .out_7(\multiplicador_mínimo_15_out_7 ), .in_2(in_2[0]));
  \multiplicador_mínimo  \multiplicador_mínimo_16  (
    .in_3(in_1[6]), .in_4(1'b0), .in_5(1'b0), .out_6(out_4[10]), .in_1(\multiplicador_mínimo_15_out_7 ),
    .out_7(out_4[11]), .in_2(in_2[0]));

  assign out_4[1:0] = 2'b00;

  // Other names for the same wires on the sheet: a0 = in_1[0]; a1 = in_1[1]; a2 = in_1[2]; a3 = in_1[3]; a4 = in_1[4];
  //   a5 = in_1[5]; a6 = in_1[6]; a7 = in_1[7]; b0 = in_2[0]; b1 = in_2[1]; b2 = in_2[2]; b3 = in_2[3]; b4 = in_2[4];
  //   b5 = in_2[5]; b6 = in_2[6]; b7 = in_2[7]
endmodule

module meio_somador (
  input  A,
  input  B,
  output S,
  output Cout
);

  xor xor_1 (S, A, B);
  and and_1 (Cout, A, B);
endmodule

module somador_completo (
  input  Cin,
  input  A,
  input  B,
  output S,
  output Cout
);

  wire MS_2_cout, MS_2_s, MS_cout;

  meio_somador MS (.A(Cin), .B(MS_2_s), .S(S), .Cout(MS_cout));
  meio_somador MS_2 (.A(A), .B(B), .S(MS_2_s), .Cout(MS_2_cout));
  or or_1 (Cout, MS_cout, MS_2_cout);
endmodule

module \multiplicador_mínimo  (
  input  in_1,
  input  in_2,
  input  in_3,
  input  in_4,
  input  in_5,
  output out_6,
  output out_7
);

  wire and_1_out, and_2_out;

  and and_1 (and_1_out, in_2, in_3);
  and and_2 (and_2_out, in_4, in_5);
  somador_completo somador_completo_1 (.Cin(in_1), .A(and_1_out), .B(and_2_out), .S(out_6), .Cout(out_7));
endmodule
